# Fritzing sketch UAS_Birru_PRG (saved by Fritzing 0.9.3b)
circuit board: 8.46667cm x 5.64444cm
breadboards: 1

parts:
  J1 = DHT11 basic temperature-humidity sensor [form="♂ (male)" package=THT]
  WeMos_D1_Mini1 = WeMos D1 Mini

nets:
  VCC: J1.VCC, WeMos_D1_Mini1.3V3
  N1: J1.OUT, WeMos_D1_Mini1.D5
  N2: J1.GND, WeMos_D1_Mini1.G

custom parts:
  DHT11 basic temperature-humidity sensor: The DHT11 is a basic, ultra low-cost digital temperature and humidity sensor. It uses a capacitive humidity sensor and a thermistor to measure the surrounding air, and spits out a digital signal on the data pin (no analog input pins needed). Its fairly simple to use, but requires careful timing to grab data. The only real downside of this sensor is you can only get new data from it once every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
